# Fritzing sketch Projeto06 (saved by Fritzing 0.9.3b)
breadboards: 1

parts:
  Mod1 = Raspberry Pi Pico
  OLED_I2C1 = OLED 128x64 I2C Monochrome Display
  hc-sr1 = hc-sr04

nets:
  GND: Mod1.pin_3, Mod1.pin_8, Mod1.pin_13, Mod1.pin_18, Mod1.pin_23, Mod1.pin_28, Mod1.pin_33, Mod1.pin_38, OLED_I2C1.GND, hc-sr1.GND
  N1: Mod1.pin_4, hc-sr1.Echo
  N2: Mod1.pin_5, hc-sr1.Trig
  N3: Mod1.pin_21, OLED_I2C1.SDA
  N4: Mod1.pin_22, OLED_I2C1.SCK
  VDD: Mod1.pin_36, OLED_I2C1.VDD, hc-sr1.VCC

custom parts:
  Raspberry Pi Pico: Raspberry Pi Pico. Based around the RP2040 microcontroller the Pico is a low cost microcontroller device bringing Raspberry Pi quality, cost, and easy of use to the microcontroller space. Jan 2021, Split part in to two versions: SMD (this one) and tht. This one is single sided and uses the castellation pads to solder the module to the board (no holes, other than for the USB connector!). The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
